# Fritzing sketch Night_Flush_Project (saved by Fritzing 1.0.3b)
breadboards: 3

parts:
  Mod1 = Raspberry Pi Pico W
  Part4 = KY-015 Temperature & Humidity Sensor Module [package="Breakout board"]
  Mod2 = Raspberry Pi Pico W
  Part5 = KY-015 Temperature & Humidity Sensor Module [package="Breakout board"]
  Mod3 = Raspberry Pi Pico W
  Mod4 = KY-011 Two Color LED Module [package="Breakout board"]
  Part6 = KY-003 Hall Magnetic Sensor Module [package="Breakout board"]

nets:
  N1: Mod1.pin_3, Mod1.pin_8, Mod1.pin_13, Mod1.pin_18, Mod1.pin_23, Mod1.pin_28, Mod1.pin_33, Mod1.pin_38, Part6.-
  N2: Mod1.pin_32, Part6.S
  N3: Mod1.pin_36, Part6.Vin
  N4: Part4.S, Mod2.pin_32
  N5: Part4.Vin, Mod2.pin_36
  N6: Part4.-, Mod2.pin_3, Mod2.pin_8, Mod2.pin_13, Mod2.pin_18, Mod2.pin_23, Mod2.pin_28, Mod2.pin_33, Mod2.pin_38, Mod4.-
  N7: Mod2.pin_29, Mod4.Vin
  N8: Mod2.pin_31, Mod4.S
  N9: Part5.S, Mod3.pin_32
  N10: Part5.Vin, Mod3.pin_36
  N11: Part5.-, Mod3.pin_3, Mod3.pin_8, Mod3.pin_13, Mod3.pin_18, Mod3.pin_23, Mod3.pin_28, Mod3.pin_33, Mod3.pin_38

notes:
  IMPORTANT!
  Your Sensors might differ from the one shown here. Allways read the datasheet specifications of your sensors
  Master - indoor
  Raspberry pi pico WH
  Temperature and humidity sensor (DH11).
  Red-green LED 3 mm
  Here happens the logic, it sends and subscribes to MQTT feeds.
  Sends MQTT feeds every 5 minutes to Adafruit
  Raspberry pi pico WH
  Hall Sensor
  This will sense if the window is open or closed. When the window is closed a magnet is in near contact with the sensor. When opening the window the magnet is out of reach.
  An MQTT feed is sent when there is a status change.
  Outdoor
  Raspberry pi pico WH
  Temperature and humidity sensor (DH11).
  Sends MQTT feeds every 5 minutes to Adafruit

custom parts:
  Raspberry Pi Pico W: Raspberry Pi Pico W. Based around the RP2040 microcontroller the Pico W is a low cost microcontroller device bringing Raspberry Pi quality, cost, and easy of use to the microcontroller space. The areas marked KEEPOUT in pcb silkscreen should not have traces running through them to avoid shorts on a soldered in module!
  KY-015 Temperature & Humidity Sensor Module: DH-11 temperature and humidity sensor in KEYES KY-015 module, provides a low-latency serial interface to measure humidity and temperature.
  KY-011 Two Color LED Module: KY-011 Two Color LED Module consist of a common cathode 3mm red/green LED.
  KY-003 Hall Magnetic Sensor Module: KEYES KY-003 Arduino Hall Magnetic Sensor Module is a switch that will turn on/off in the presence of a magnetic field.
